# Fritzing sketch schem (saved by Fritzing 0.9.3b)

parts:
  Part1 = Arduino Nano (Rev3.0)
  Mod1 = KY-019 5V Relay Module [package="Breakout board"]
  Mod2 = KY-019 5V Relay Module [package="Breakout board"]
  Part2 = TM1637
  RE1 = KY-040 Rotary encoder [package=THT]
  buz1 = Piezo Buzzer

nets:
  N1: Part1.D2, Mod2.S
  N2: Part1.D4, RE1.CLK
  N3: Part1.D5, RE1.DT
  N4: Part1.D6, RE1.SW
  N5: Part1.D7, Part2.CLK
  N6: Part1.D8, Part2.DIO
  N7: Part1.D9, Mod1.S
  N8: Part1.D11/MOSI, buz1.pin_1
  N9: Mod1.+, Part2.GND
  N10: Mod2.-, Part2.VCC

custom parts:
  KY-019 5V Relay Module: KY-019 5V Relay module, used to control AC circuits.
  TM1637: A 4 7-seg display
  KY-040 Rotary encoder: KY-040 Rotary Encoder with switch on breakout borad from AZ Delivery
  Piezo Buzzer: Part from https://www.nutsvolts.com/magazine/article/november2012_SmileysWorkshop modified to be .3 in spacing to match the adafruit buzzer 5V breadboard friendly part.
